# Fritzing sketch exemplo-02-programacao (saved by Fritzing 0.9.3b)
breadboards: 1

parts:
  Componente1 = Arduino Uno (Rev3)
  LED1 = smd LED [color="Red (633nm)" package="0603 [SMD]"]
  R1 = Resistor [tolerance=±5% resistance=220 package=THT]

nets:
  N1: Componente1.D11_PWM/MOSI, R1.Pin_1
  N2: Componente1.GND, LED1.cathode
  N3: LED1.anode, R1.Pin_0
