# Fritzing sketch projeto-02-potenciometro (saved by Fritzing 0.9.3b)
breadboards: 1

parts:
  U1 = POT [package=pot_alpha_rv16af-20]
  LED1 = smd LED [color="Red (633nm)" package="0603 [SMD]"]
  R1 = Resistor [tolerance=±5% resistance=220 package=THT]
  Componente1 = Arduino Uno (Rev3)

nets:
  N1: U1.A, LED1.cathode, Componente1.GND
  N2: U1.S, Componente1.A0
  N3: U1.E, Componente1.5V
  N4: LED1.anode, R1.Pin_1
  N5: R1.Pin_0, Componente1.D11_PWM/MOSI
