# Fritzing sketch projeto-02-programacao (saved by Fritzing 0.9.3b)
breadboards: 1

parts:
  LED1 = smd LED [color="Red (633nm)" package="0603 [SMD]"]
  R1 = Resistor [tolerance=±5% resistance=220 package=THT]
  Componente1 = Arduino Uno (Rev3)

nets:
  N1: LED1.cathode, Componente1.GND
  N2: LED1.anode, R1.Pin_1
  N3: R1.Pin_0, Componente1.D11_PWM/MOSI
