# Fritzing sketch projeto-04 (saved by Fritzing 0.9.3b)
breadboards: 1

parts:
  Componente1 = Arduino Uno (Rev3)
  R1 = Resistor [tolerance=±5% resistance=220 package=THT]
  LED1 = smd LED [color="Red (633nm)" package="0603 [SMD]"]
  LED2 = smd LED [color="Yellow (595nm)" package="0603 [SMD]"]
  LED3 = smd LED [color="Green (555nm)" package="0603 [SMD]"]
  R2 = Resistor [tolerance=±5% resistance=220 package=THT]
  R3 = Resistor [tolerance=±5% resistance=220 package=THT]

nets:
  N1: Componente1.D11_PWM/MOSI, R3.Pin_1
  N2: Componente1.D12/MISO, R2.Pin_1
  N3: Componente1.D13/SCK, R1.Pin_1
  N4: Componente1.GND, LED1.cathode, LED2.cathode, LED3.cathode
  N5: R1.Pin_0, LED1.anode
  N6: LED2.anode, R2.Pin_0
  N7: LED3.anode, R3.Pin_0
