# Fritzing sketch exemplo-06 (saved by Fritzing 0.9.3b)
breadboards: 1

parts:
  Componente1 = Arduino Uno (Rev3)
  J1 = Piezo Speaker

nets:
  N1: Componente1.D11_PWM/MOSI, J1.pin2
  N2: Componente1.GND, J1.pin1
