# Fritzing sketch projeto-08 (saved by Fritzing 0.9.3b)
breadboards: 2

parts:
  U1 = POT [package=pot_alpha_rv16af-20]
  Componente1 = Arduino Uno (Rev3)
  U3 = LCD-16X2 [package=lcd-16x2]
  DHT2 = DHT11 Humitidy and Temperature Sensor
  R1 = Photocell (LDR) [package=THT]
  R2 = Resistor [tolerance=±5% resistance=220 package="0603 [SMD]"]

nets:
  VDD: U1.A, Componente1.5V, U3.VDD, U3.A, DHT2.VDD, R1.pin_0
  N1: U1.S, U3.VO
  GND: U1.E, Componente1.GND, U3.VSS, U3.R_W, U3.K, DHT2.GND, R2.Pin_1
  N2: Componente1.A0, DHT2.DATA
  N3: Componente1.A1, R1.pin_1, R2.Pin_0
  N4: Componente1.D2, U3.RS
  N5: Componente1.D3_PWM, U3.E
  N6: Componente1.D4, U3.DB4
  N7: Componente1.D5_PWM, U3.DB5
  N8: Componente1.D6_PWM, U3.DB6
  N9: Componente1.D7, U3.DB7

custom parts:
  DHT11 Humitidy and Temperature Sensor: DHT11 Humidity and Temperature Sensor
